// Logisim project 16 bit computer.circ as structural Verilog
module CPU (
  output [7:0] out_1,
  output [7:0] out_2,
  output [7:0] out_3,
  output [7:0] out_4,
  output [7:0] out_5,
  output [7:0] out_6,
  output [7:0] out_7,
  output [7:0] out_8,
  output [7:0] out_9,
  output [7:0] out_10
);

  wire clock_1_out, jmp_a_out, mov_ah_value8_out, mov_al_value8_out, mov_ax_value16_out, mov_bh_value8_out,
       mov_bl_value8_out, mov_bx_value16_out, mov_ch_value8_out, mov_cl_value8_out, mov_cx_value16_out,
       mov_dh_value8_out, mov_dl_value8_out, mov_dx_value16_out, mov_sp_value16_out, mov_sph_value8_out,
       mov_spl_value8_out;
  wire [7:0] ram_1_data;
  wire [15:0] ip_register_small_1_ip;

  ip_Register_small ip_register_small_1 (
    .mov_ip_value16(jmp_a_out), .Data_In({out_1, out_2}), .CLK(clock_1_out), .ip(ip_register_small_1_ip));
  Clock clock_1 (.out(clock_1_out));
  RAM #(.addrWidth(16)) ram_1 (
    .addr(ip_register_small_1_ip), .data(ram_1_data), .clk(clock_1_out));  // open: sel, ld, clr
  and mov_ax_value16 (mov_ax_value16_out, ram_1_data[0], ~ram_1_data[1], ~ram_1_data[2], ~ram_1_data[3], ~ram_1_data[4], ~ram_1_data[5], ~ram_1_data[6], ~ram_1_data[7]);  // AND_Gate
  and mov_bx_value16 (mov_bx_value16_out, ~ram_1_data[0], ram_1_data[1], ~ram_1_data[2], ~ram_1_data[3], ~ram_1_data[4], ~ram_1_data[5], ~ram_1_data[6], ~ram_1_data[7]);  // AND_Gate
  and mov_cx_value16 (mov_cx_value16_out, ram_1_data[0], ram_1_data[1], ~ram_1_data[2], ~ram_1_data[3], ~ram_1_data[4], ~ram_1_data[5], ~ram_1_data[6], ~ram_1_data[7]);  // AND_Gate
  and mov_dx_value16 (mov_dx_value16_out, ~ram_1_data[0], ~ram_1_data[1], ram_1_data[2], ~ram_1_data[3], ~ram_1_data[4], ~ram_1_data[5], ~ram_1_data[6], ~ram_1_data[7]);  // AND_Gate
  and mov_sp_value16 (mov_sp_value16_out, ram_1_data[0], ~ram_1_data[1], ram_1_data[2], ~ram_1_data[3], ~ram_1_data[4], ~ram_1_data[5], ~ram_1_data[6], ~ram_1_data[7]);  // AND_Gate
  and mov_al_value8 (mov_al_value8_out, ~ram_1_data[0], ram_1_data[1], ram_1_data[2], ~ram_1_data[3], ~ram_1_data[4], ~ram_1_data[5], ~ram_1_data[6], ~ram_1_data[7]);  // AND_Gate
  and mov_ah_value8 (mov_ah_value8_out, ram_1_data[0], ram_1_data[1], ram_1_data[2], ~ram_1_data[3], ~ram_1_data[4], ~ram_1_data[5], ~ram_1_data[6], ~ram_1_data[7]);  // AND_Gate
  and mov_bl_value8 (mov_bl_value8_out, ~ram_1_data[0], ~ram_1_data[1], ~ram_1_data[2], ram_1_data[3], ~ram_1_data[4], ~ram_1_data[5], ~ram_1_data[6], ~ram_1_data[7]);  // AND_Gate
  and mov_bh_value8 (mov_bh_value8_out, ram_1_data[0], ~ram_1_data[1], ~ram_1_data[2], ram_1_data[3], ~ram_1_data[4], ~ram_1_data[5], ~ram_1_data[6], ~ram_1_data[7]);  // AND_Gate
  and mov_cl_value8 (mov_cl_value8_out, ~ram_1_data[0], ram_1_data[1], ~ram_1_data[2], ram_1_data[3], ~ram_1_data[4], ~ram_1_data[5], ~ram_1_data[6], ~ram_1_data[7]);  // AND_Gate
  and mov_ch_value8 (mov_ch_value8_out, ram_1_data[0], ram_1_data[1], ~ram_1_data[2], ram_1_data[3], ~ram_1_data[4], ~ram_1_data[5], ~ram_1_data[6], ~ram_1_data[7]);  // AND_Gate
  and mov_dl_value8 (mov_dl_value8_out, ~ram_1_data[0], ~ram_1_data[1], ram_1_data[2], ram_1_data[3], ~ram_1_data[4], ~ram_1_data[5], ~ram_1_data[6], ~ram_1_data[7]);  // AND_Gate
  and mov_dh_value8 (mov_dh_value8_out, ram_1_data[0], ~ram_1_data[1], ram_1_data[2], ram_1_data[3], ~ram_1_data[4], ~ram_1_data[5], ~ram_1_data[6], ~ram_1_data[7]);  // AND_Gate
  and mov_spl_value8 (mov_spl_value8_out, ~ram_1_data[0], ram_1_data[1], ram_1_data[2], ram_1_data[3], ~ram_1_data[4], ~ram_1_data[5], ~ram_1_data[6], ~ram_1_data[7]);  // AND_Gate
  and mov_sph_value8 (mov_sph_value8_out, ram_1_data[0], ram_1_data[1], ram_1_data[2], ram_1_data[3], ~ram_1_data[4], ~ram_1_data[5], ~ram_1_data[6], ~ram_1_data[7]);  // AND_Gate
  and jmp_a (jmp_a_out, ~ram_1_data[0], ~ram_1_data[1], ~ram_1_data[2], ~ram_1_data[3], ram_1_data[4], ~ram_1_data[5], ~ram_1_data[6], ~ram_1_data[7]);  // AND_Gate
  _16_Bit_Register ax (
    .mov_ax_value16(mov_ax_value16_out), .mov_ah_value8(mov_ah_value8_out),
    .mov_al_value8(mov_al_value8_out), .Data(ram_1_data), .CLK(clock_1_out), .ah(out_1), .al(out_2));
  _16_Bit_Register bx (
    .mov_ax_value16(mov_bx_value16_out), .mov_ah_value8(mov_bh_value8_out),
    .mov_al_value8(mov_bl_value8_out), .Data(ram_1_data), .CLK(clock_1_out), .ah(out_3), .al(out_4));
  _16_Bit_Register cx (
    .mov_ax_value16(mov_cx_value16_out), .mov_ah_value8(mov_ch_value8_out),
    .mov_al_value8(mov_cl_value8_out), .Data(ram_1_data), .CLK(clock_1_out), .ah(out_5), .al(out_6));
  _16_Bit_Register dx (
    .mov_ax_value16(mov_dx_value16_out), .mov_ah_value8(mov_dh_value8_out),
    .mov_al_value8(mov_dl_value8_out), .Data(ram_1_data), .CLK(clock_1_out), .ah(out_7), .al(out_8));
  _16_Bit_Register sp (
    .mov_ax_value16(mov_sp_value16_out), .mov_ah_value8(mov_sph_value8_out),
    .mov_al_value8(mov_spl_value8_out), .Data(ram_1_data), .CLK(clock_1_out), .ah(out_9), .al(out_10));
endmodule

module Register_small (
  input  mov_ah_value8,
  input  mov_al_value8,
  input  [7:0] Data_In,
  input  CLK,
  output [7:0] ah,
  output [7:0] al
);

  wire [7:0] transistor_1_out, transistor_2_out;

  Transistor #(.\type ("n"), .width(8)) transistor_1 (.in(Data_In), .out(transistor_1_out), .gate(mov_ah_value8));
  Transistor #(.\type ("n"), .width(8)) transistor_2 (.in(Data_In), .out(transistor_2_out), .gate(mov_al_value8));
  Register_part u_ah (.D(transistor_1_out), .en(mov_ah_value8), .Q(ah), .clk(CLK));  // open: clr
  Register_part u_al (.D(transistor_2_out), .en(mov_al_value8), .Q(al), .clk(CLK));  // open: clr
endmodule

module _2_cycle (
  input  Active,
  input  CLK,
  output Trigger
);

  wire and_1_out, d_ff_1_qn, or_1_out, t_ff_1_q;

  D_Flip_Flop d_ff_1 (
    .clk(CLK), .D(and_1_out), .Q(Trigger), .Qn(d_ff_1_qn), .en(or_1_out), .reset(t_ff_1_q));  // open: preset
  and and_1 (and_1_out, ~Trigger, Active);  // AND_Gate
  or or_1 (or_1_out, and_1_out, t_ff_1_q);
  T_Flip_Flop t_ff_1 (.clk(CLK), .T(Trigger), .Q(t_ff_1_q), .reset(d_ff_1_qn), .en(CLK));  // open: Qn, preset
endmodule

module _3_cycle (
  input  Active,
  input  CLK,
  output _1,
  output _2,
  output _3
);

  wire and_1_out, and_2_out, and_3_out, or_1_out;

  and and_1 (and_1_out, ~or_1_out, Active);  // AND_Gate
  D_Flip_Flop d_ff_1 (.clk(CLK), .D(and_2_out), .Q(_1));  // open: Qn, preset, en, reset
  and and_2 (and_2_out, ~_1, and_1_out);  // AND_Gate
  T_Flip_Flop t_ff_1 (.clk(CLK), .T(_1), .Q(_2), .reset(and_3_out), .en(CLK));  // open: Qn, preset
  and and_3 (and_3_out, _2, _3);
  or or_1 (or_1_out, _1, _2);
  D_Flip_Flop d_ff_2 (.clk(CLK), .D(_2), .Q(_3));  // open: Qn, preset, en, reset
endmodule

module _16_Bit_Register (
  input  mov_ax_value16,
  input  mov_ah_value8,
  input  mov_al_value8,
  input  [7:0] Data,
  input  CLK,
  output [7:0] ah,
  output [7:0] al
);

  wire n2_cycle_1_trigger, n2_cycle_2_trigger, n3_cycle_1__1, or_1_out, or_2_out, or_3_out;
  wire [7:0] transistor_1_out;

  or or_1 (or_1_out, mov_ax_value16, mov_ah_value8);
  or or_2 (or_2_out, n3_cycle_1__1, mov_al_value8);
  _3_cycle u_3_cycle_1 (.Active(mov_ax_value16), .CLK(CLK), ._1(n3_cycle_1__1));  // open: _2, _3
  _2_cycle u_2_cycle_1 (.Active(or_1_out), .CLK(CLK), .Trigger(n2_cycle_1_trigger));
  _2_cycle u_2_cycle_2 (.Active(or_2_out), .CLK(CLK), .Trigger(n2_cycle_2_trigger));
  or or_3 (or_3_out, n2_cycle_1_trigger, n2_cycle_2_trigger);
  Transistor #(.\type ("n"), .width(8)) transistor_1 (.in(Data), .out(transistor_1_out), .gate(or_3_out));
  Register_small ax (
    .mov_ah_value8(n2_cycle_1_trigger), .mov_al_value8(n2_cycle_2_trigger), .Data_In(transistor_1_out),
    .CLK(CLK), .ah(ah), .al(al));
endmodule

module ip_Register (
  input  mov_ip_value16,
  input  mov_iph_value8,
  input  mov_ipl_value8,
  input  [7:0] Data,
  input  CLK,
  output out_6,
  output [7:0] ah,
  output [7:0] al
);

  wire n2_cycle_1_trigger, n2_cycle_2_trigger, n3_cycle_1__1, or_1_out, or_2_out, or_3_out;
  wire [7:0] transistor_1_out;

  or or_1 (or_1_out, mov_ip_value16, mov_iph_value8);
  or or_2 (or_2_out, n3_cycle_1__1, mov_ipl_value8);
  _3_cycle u_3_cycle_1 (.Active(mov_ip_value16), .CLK(CLK), ._1(n3_cycle_1__1));  // open: _2, _3
  _2_cycle u_2_cycle_1 (.Active(or_1_out), .CLK(CLK), .Trigger(n2_cycle_1_trigger));
  _2_cycle u_2_cycle_2 (.Active(or_2_out), .CLK(CLK), .Trigger(n2_cycle_2_trigger));
  or or_3 (or_3_out, n2_cycle_1_trigger, n2_cycle_2_trigger);
  Transistor #(.\type ("n"), .width(8)) transistor_1 (.in(Data), .out(transistor_1_out), .gate(or_3_out));
  or or_4 (out_6, n2_cycle_2_trigger, n2_cycle_1_trigger);
  Register_small ax (
    .mov_ah_value8(n2_cycle_1_trigger), .mov_al_value8(n2_cycle_2_trigger), .Data_In(transistor_1_out),
    .CLK(CLK), .ah(ah), .al(al));
endmodule

module ip_Register_small (
  input  mov_ip_value16,
  input  [15:0] Data_In,
  input  CLK,
  output [15:0] ip
);

  wire not_1_out;

  not not_1 (not_1_out, mov_ip_value16);
  Counter #(.width(16), .max('hffff), .trigger("falling")) counter_1 (
    .load(mov_ip_value16), .D(Data_In), .count(not_1_out), .Q(ip), .clk(CLK));  // open: carry, clr
endmodule

module Register_Block (
);

  Register_small ax ();  // open: mov_ah_value8, mov_al_value8, Data_In, CLK, ah, al
  Register_small bx ();  // open: mov_ah_value8, mov_al_value8, Data_In, CLK, ah, al
  Register_small cx ();  // open: mov_ah_value8, mov_al_value8, Data_In, CLK, ah, al
  Register_small dx ();  // open: mov_ah_value8, mov_al_value8, Data_In, CLK, ah, al
  Register_small sp ();  // open: mov_ah_value8, mov_al_value8, Data_In, CLK, ah, al
endmodule

module Register (
  input  mov_reg_value16,
  input  mov_highbyte_value8,
  input  mov_lowbyte_value8,
  input  [7:0] value8_in,
  input  [15:0] value16_in,
  input  CLK,
  output [15:0] value16,
  output [7:0] High_Byte,
  output [7:0] Low_Byte
);

  wire or_1_out, or_2_out;
  wire [7:0] or_3_out, or_4_out, transistor_2_out;
  wire [15:0] transistor_1_out;

  Transistor #(.\type ("n"), .width(16)) transistor_1 (.in(value16_in), .out(transistor_1_out), .gate(mov_reg_value16));
  Transistor #(.width(8)) transistor_2 (.in(value8_in), .out(transistor_2_out), .gate(mov_reg_value16));
  or or_1 (or_1_out, mov_reg_value16, mov_lowbyte_value8);
  or or_2 (or_2_out, mov_reg_value16, mov_highbyte_value8);
  assign or_3_out = transistor_2_out | transistor_1_out[7:0];  // OR_Gate or_3, 8 bits wide
  assign or_4_out = transistor_2_out | transistor_1_out[15:8];  // OR_Gate or_4, 8 bits wide
  Register_part u_low_byte (.D(or_3_out), .en(or_1_out), .Q(Low_Byte), .clk(CLK));  // open: clr
  Register_part u_high_byte (.D(or_4_out), .en(or_2_out), .Q(High_Byte), .clk(CLK));  // open: clr

  assign value16 = {High_Byte, Low_Byte};
endmodule

module RegisterPlusAnd (
  input  CLK,
  input  d0,
  input  in_3,
  input  in_4,
  input  in_5,
  input  in_6,
  input  in_7,
  input  in_8,
  input  d7,
  output [7:0] out_10,
  output [7:0] out_11,
  output [7:0] out_12,
  output [7:0] out_13,
  output [7:0] out_14,
  output [7:0] out_15,
  output [7:0] out_16,
  output [7:0] out_17,
  output [7:0] out_18,
  output [7:0] out_19
);

  _16_Bit_Register ax (
    .Data({d7, in_8, in_7, in_6, in_5, in_4, in_3, d0}), .CLK(CLK), .ah(out_10), .al(out_11));  // open: mov_ax_value16, mov_ah_value8, mov_al_value8
  _16_Bit_Register bx (
    .Data({d7, in_8, in_7, in_6, in_5, in_4, in_3, d0}), .CLK(CLK), .ah(out_12), .al(out_13));  // open: mov_ax_value16, mov_ah_value8, mov_al_value8
  _16_Bit_Register cx (
    .Data({d7, in_8, in_7, in_6, in_5, in_4, in_3, d0}), .CLK(CLK), .ah(out_14), .al(out_15));  // open: mov_ax_value16, mov_ah_value8, mov_al_value8
  _16_Bit_Register dx (
    .Data({d7, in_8, in_7, in_6, in_5, in_4, in_3, d0}), .CLK(CLK), .ah(out_16), .al(out_17));  // open: mov_ax_value16, mov_ah_value8, mov_al_value8
  _16_Bit_Register sp (
    .Data({d7, in_8, in_7, in_6, in_5, in_4, in_3, d0}), .CLK(CLK), .ah(out_18), .al(out_19));  // open: mov_ax_value16, mov_ah_value8, mov_al_value8
endmodule

module _16_bit_Reg (
  input  CLK,
  input  mov_reg_value16,
  input  mov_regh_value8,
  input  mov_regl_value8,
  input  [7:0] Data,
  output reg_write,
  output [7:0] regh,
  output [7:0] regl
);

  wire d_ff_1_q, d_ff_2_q, d_ff_3_q, d_ff_4_q, or_1_out, or_3_out;

  D_Flip_Flop d_ff_1 (.clk(CLK), .D(mov_regh_value8), .Q(d_ff_1_q));  // open: Qn, preset, en, reset
  D_Flip_Flop d_ff_2 (.clk(CLK), .D(mov_regl_value8), .Q(d_ff_2_q));  // open: Qn, preset, en, reset
  D_Flip_Flop d_ff_3 (.clk(CLK), .D(mov_reg_value16), .Q(d_ff_3_q));  // open: Qn, preset, en, reset
  or or_1 (or_1_out, d_ff_3_q, d_ff_2_q);
  D_Flip_Flop d_ff_4 (.clk(CLK), .D(d_ff_3_q), .Q(d_ff_4_q));  // open: Qn, preset, en, reset
  or or_2 (reg_write, or_1_out, or_3_out);
  or or_3 (or_3_out, d_ff_4_q, d_ff_1_q);
  Register_part u_regh (.D(Data), .en(or_3_out), .Q(regh), .clk(CLK));  // open: clr
  Register_part u_regl (.D(Data), .en(or_1_out), .Q(regl), .clk(CLK));  // open: clr
endmodule

module CPU_2 (
  input  write,
  input  [7:0] in_2,
  input  in_3,
  input  in_4,
  input  [15:0] in_5,
  input  in_6,
  input  enable,
  input  in_8,
  input  in_9,
  input  [7:0] in_10,
  input  [7:0] in_11,
  output [7:0] out_12,
  output [7:0] out_13,
  output [7:0] out_14,
  output [7:0] out_15,
  output [7:0] out_16,
  output [7:0] out_17,
  output [7:0] out_18,
  output [7:0] out_19,
  output [7:0] out_20,
  output [7:0] out_21,
  output [7:0] out_22
);

  wire clock_1_out, counter_2_carry, counter_3_carry, counter_4_carry, d_ff_1_q, decoder_1_mov_ax_value16,
       decoder_1_mov_bx_value16, or_2_out, undriven, undriven_2, undriven_3, undriven_4, undriven_5,
       undriven_6;
  wire [7:0] counter_2_q, counter_3_q, counter_4_q, decoder_1_data_out, or_1_out;
  wire [15:0] counter_1_q;

  Clock clock_1 (.out(clock_1_out));
  Counter #(.width(16), .max('hffff)) counter_1 (
    .load(in_3), .D(in_5), .count(in_6), .Q(counter_1_q), .clk(clock_1_out));  // open: carry, clr
  assign or_1_out = in_11 | in_11;  // OR_Gate or_1, 8 bits wide
  RAM #(.addrWidth(16), .bus("separate")) ram_1 (
    .addr(counter_1_q), .din(or_1_out), .data(in_2), .str(in_8), .sel(enable), .clk(clock_1_out), .ld(in_9));  // open: clr
  Decoder decoder_1 (
    .CLK(clock_1_out), .data_in(in_10), .data_out(decoder_1_data_out),
    .mov_ax_value16(decoder_1_mov_ax_value16), .mov_bx_value16(decoder_1_mov_bx_value16));  // open: mov_cx_value16, mov_dx_value16, mov_dx_value16_2
  Counter counter_2 (
    .load(undriven), .D(in_2), .count(undriven_2), .Q(counter_2_q), .carry(counter_2_carry), .clk(write));  // open: clr
  Counter counter_3 (
    .load(undriven_3), .D(in_2), .count(undriven_4), .Q(counter_3_q), .carry(counter_3_carry), .clk(write));  // open: clr
  Counter counter_4 (
    .load(undriven_5), .D(in_2), .count(undriven_6), .Q(counter_4_q), .carry(counter_4_carry), .clk(write));  // open: clr
  or or_2 (or_2_out, in_4, in_4);
  _16_bit_Reg ax (
    .CLK(clock_1_out), .mov_reg_value16(decoder_1_mov_ax_value16), .Data(decoder_1_data_out), .regh(out_13),
    .regl(out_14));  // open: mov_regh_value8, mov_regl_value8, reg_write
  _16_bit_Reg bx (
    .CLK(clock_1_out), .mov_reg_value16(decoder_1_mov_bx_value16), .Data(decoder_1_data_out), .regh(out_15),
    .regl(out_16));  // open: mov_regh_value8, mov_regl_value8, reg_write
  _16_bit_Reg cx (
    .regh(out_17), .regl(out_18));  // open: CLK, mov_reg_value16, mov_regh_value8, mov_regl_value8, Data, reg_write
  _16_bit_Reg dx (
    .regh(out_19), .regl(out_20));  // open: CLK, mov_reg_value16, mov_regh_value8, mov_regl_value8, Data, reg_write
  _16_bit_Reg sp (
    .regh(out_21), .regl(out_22));  // open: CLK, mov_reg_value16, mov_regh_value8, mov_regl_value8, Data, reg_write
  D_Flip_Flop d_ff_1 (.clk(clock_1_out), .D(or_2_out), .Q(d_ff_1_q));  // open: Qn, preset, en, reset
  RAM #(.addrWidth(24), .bus("separate")) ram_2 (
    .addr({counter_4_q, counter_3_q, counter_2_q}), .sel(d_ff_1_q), .clk(clock_1_out));  // open: din, data, str, ld, clr

  assign out_12 = in_2;

  // Notes on the sheet:
  //   Program execute/program read write memory
  //   24 bit memory for graphics
endmodule

module RAM_Interface (
  input  CLK,
  input  load,
  input  store,
  input  [7:0] data_in,
  output [7:0] data_out
);

  Counter #(.width(16), .max('hffff)) counter_1 ();  // open: load, D, count, Q, carry, clk, clr
  RAM #(.addrWidth(16), .bus("separate")) ram_1 (.clk(CLK));  // open: addr, din, data, str, sel, ld, clr
endmodule

module Decoder (
  input  CLK,
  input  [7:0] data_in,
  output [7:0] data_out,
  output mov_ax_value16,
  output mov_bx_value16,
  output mov_cx_value16,
  output mov_dx_value16,
  output mov_dx_value16_2
);

  wire and_1_out, exec_q, mov_ax_value16_out, mov_bx_value16_out, mov_cx_value16_out, mov_dx_value16_out,
       mov_sp_value16_out, n3_cycle_1__1, n3_cycle_1__2, n3_cycle_1__3, or_1_out, or_2_out;

  and u_mov_ax_value16 (mov_ax_value16_out, data_in[0], ~data_in[1], ~data_in[2], ~data_in[3], ~data_in[4], ~data_in[5], ~data_in[6], ~data_in[7]);  // AND_Gate
  and u_mov_bx_value16 (mov_bx_value16_out, ~data_in[0], data_in[1], ~data_in[2], ~data_in[3], ~data_in[4], ~data_in[5], ~data_in[6], ~data_in[7]);  // AND_Gate
  and u_mov_cx_value16 (mov_cx_value16_out, data_in[0], data_in[1], ~data_in[2], ~data_in[3], ~data_in[4], ~data_in[5], ~data_in[6], ~data_in[7]);  // AND_Gate
  and u_mov_dx_value16 (mov_dx_value16_out, ~data_in[0], ~data_in[1], data_in[2], ~data_in[3], ~data_in[4], ~data_in[5], ~data_in[6], ~data_in[7]);  // AND_Gate
  and mov_sp_value16 (mov_sp_value16_out, data_in[0], ~data_in[1], data_in[2], ~data_in[3], ~data_in[4], ~data_in[5], ~data_in[6], ~data_in[7]);  // AND_Gate
  D_Flip_Flop #(.trigger("high")) exec (.clk(CLK), .D(or_2_out), .Q(exec_q));  // open: Qn, preset, en, reset
  and and_1 (and_1_out, or_1_out, ~n3_cycle_1__1, ~n3_cycle_1__2, ~1'b0);  // AND_Gate
  or or_1 (or_1_out, mov_ax_value16_out, mov_bx_value16_out, mov_cx_value16_out, mov_dx_value16_out, mov_sp_value16_out);
  _3_cycle u_3_cycle_1 (.Active(and_1_out), .CLK(CLK), ._1(n3_cycle_1__1), ._2(n3_cycle_1__2), ._3(n3_cycle_1__3));
  or or_2 (or_2_out, n3_cycle_1__1, n3_cycle_1__2);
  and and_2 (mov_ax_value16, ~exec_q, mov_ax_value16_out);  // AND_Gate
  and and_3 (mov_bx_value16, ~exec_q, mov_bx_value16_out);  // AND_Gate
  and and_4 (mov_cx_value16, ~exec_q, mov_cx_value16_out);  // AND_Gate
  and and_5 (mov_dx_value16, ~exec_q, mov_dx_value16_out);  // AND_Gate
  and and_6 (mov_dx_value16_2, ~exec_q, mov_sp_value16_out);  // AND_Gate

  assign data_out = data_in;
endmodule

module CPU_BUS (
  output [15:0] BUS,
  output [15:0] Control_Lines
);

  wire bus_decoder_16_bit_bus_intruction_set_1_1_ax_enable_instruction,
       bus_decoder_16_bit_bus_intruction_set_1_1_bx_enable_instruction,
       bus_decoder_16_bit_bus_intruction_set_1_1_cx_enable_instruction,
       bus_decoder_16_bit_bus_intruction_set_1_1_dx_enable_instruction,
       bus_decoder_16_bit_bus_intruction_set_1_1_ram0_instruction_enable, CLK_out;
  wire [2:0] bus_decoder_16_bit_bus_intruction_set_1_1_ax_instruction,
       bus_decoder_16_bit_bus_intruction_set_1_1_bx_instruction,
       bus_decoder_16_bit_bus_intruction_set_1_1_cx_instruction,
       bus_decoder_16_bit_bus_intruction_set_1_1_dx_instruction;
  wire [7:0] bus_decoder_16_bit_bus_intruction_set_1_1_ram0_instruction;

  BUS_Register Reg_ax (
    .DataOut(BUS), .DataIn(BUS),
    .Instruction_Enable(bus_decoder_16_bit_bus_intruction_set_1_1_ax_enable_instruction), .CLK(CLK_out),
    .Instruction_Line(bus_decoder_16_bit_bus_intruction_set_1_1_ax_instruction));
  BUS_Register Reg_bx (
    .DataOut(BUS), .DataIn(BUS),
    .Instruction_Enable(bus_decoder_16_bit_bus_intruction_set_1_1_bx_enable_instruction), .CLK(CLK_out),
    .Instruction_Line(bus_decoder_16_bit_bus_intruction_set_1_1_bx_instruction));
  BUS_Register Reg_cx (
    .DataOut(BUS), .DataIn(BUS),
    .Instruction_Enable(bus_decoder_16_bit_bus_intruction_set_1_1_cx_enable_instruction), .CLK(CLK_out),
    .Instruction_Line(bus_decoder_16_bit_bus_intruction_set_1_1_cx_instruction));
  BUS_Register Reg_dx (
    .DataOut(BUS), .DataIn(BUS),
    .Instruction_Enable(bus_decoder_16_bit_bus_intruction_set_1_1_dx_enable_instruction), .CLK(CLK_out),
    .Instruction_Line(bus_decoder_16_bit_bus_intruction_set_1_1_dx_instruction));
  BUS_Decoder_16_bit_bus_intruction_set_1 bus_decoder_16_bit_bus_intruction_set_1_1 (
    .CLK(CLK_out), .ax_enable_instruction(bus_decoder_16_bit_bus_intruction_set_1_1_ax_enable_instruction),
    .ax_instruction(bus_decoder_16_bit_bus_intruction_set_1_1_ax_instruction),
    .bx_enable_instruction(bus_decoder_16_bit_bus_intruction_set_1_1_bx_enable_instruction),
    .bx_instruction(bus_decoder_16_bit_bus_intruction_set_1_1_bx_instruction),
    .cx_enable_instruction(bus_decoder_16_bit_bus_intruction_set_1_1_cx_enable_instruction),
    .cx_instruction(bus_decoder_16_bit_bus_intruction_set_1_1_cx_instruction),
    .dx_enable_instruction(bus_decoder_16_bit_bus_intruction_set_1_1_dx_enable_instruction),
    .dx_instruction(bus_decoder_16_bit_bus_intruction_set_1_1_dx_instruction), .Data_In(BUS),
    .RAM0_Instruction_Enable(bus_decoder_16_bit_bus_intruction_set_1_1_ram0_instruction_enable),
    .RAM0_Instruction(bus_decoder_16_bit_bus_intruction_set_1_1_ram0_instruction));  // open: Control_Line_Out
  Clock CLK (.out(CLK_out));
  BUS_ALU bus_alu_1 (.CLK(CLK_out));  // open: BUS_Out, BUS_In, Read_Write, Load_Enable, Load_Selector, Add_Sub
  BUS_RAM RAM0 (
    .Bus_Out(BUS), .Bus_In(BUS), .CLK(CLK_out),
    .RAM_Instruction(bus_decoder_16_bit_bus_intruction_set_1_1_ram0_instruction),
    .RAM_Instruction_Enable(bus_decoder_16_bit_bus_intruction_set_1_1_ram0_instruction_enable));
  BUS_RAM RAM1 (.CLK(CLK_out));  // open: Bus_Out, Bus_In, RAM_Instruction, RAM_Instruction_Enable

  // Notes on the sheet:
  //   Decoder
endmodule

module BUS_Register (
  input  [15:0] DataIn,
  input  Instruction_Enable,
  input  CLK,
  input  [2:0] Instruction_Line,
  output [15:0] DataOut
);

  wire and_1_out, and_2_out, and_3_out, and_4_out, and_5_out, and_6_out, and_7_out, and_8_out, and_9_out,
       counter_1_carry, decoder_1_out0, decoder_1_out1, decoder_1_out2, decoder_1_out3, decoder_1_out4,
       decoder_1_out5, decoder_1_out6, not_1_out, not_2_out, or_1_out, or_2_out, or_3_out, or_4_out;
  wire [7:0] counter_1_q, counter_2_q, multiplexer_1_out;
  wire [15:0] controlled_buffer_1_out;

  Decoder_part #(.select(3), .enable("false")) decoder_1 (
    .out0(decoder_1_out0), .out1(decoder_1_out1), .out2(decoder_1_out2), .out3(decoder_1_out3),
    .out4(decoder_1_out4), .out5(decoder_1_out5), .out6(decoder_1_out6), .sel(Instruction_Line));  // open: out7
  and and_1 (and_1_out, decoder_1_out0, Instruction_Enable);
  and and_2 (and_2_out, decoder_1_out1, Instruction_Enable);
  and and_3 (and_3_out, decoder_1_out2, Instruction_Enable);
  and and_4 (and_4_out, decoder_1_out3, Instruction_Enable);
  and and_5 (and_5_out, decoder_1_out4, Instruction_Enable);
  and and_6 (and_6_out, decoder_1_out5, Instruction_Enable);
  and and_7 (and_7_out, decoder_1_out6, Instruction_Enable);
  assign controlled_buffer_1_out = not_1_out ? DataIn : 16'bz;  // Controlled_Buffer controlled_buffer_1
  not not_1 (not_1_out, and_7_out);
  or or_1 (or_1_out, and_4_out, and_1_out, and_3_out);
  or or_2 (or_2_out, and_9_out, and_1_out, and_2_out);
  not not_2 (not_2_out, and_2_out);
  or or_3 (or_3_out, and_4_out, and_5_out);
  Multiplexer #(.width(8)) multiplexer_1 (
    .in0(controlled_buffer_1_out[7:0]), .in1(controlled_buffer_1_out[15:8]), .out(multiplexer_1_out),
    .sel(not_2_out), .en(1'b1));
  Counter counter_1 (
    .load(or_1_out), .D(controlled_buffer_1_out[7:0]), .count(or_3_out), .Q(counter_1_q),
    .carry(counter_1_carry), .clk(CLK), .clr(and_6_out));
  and and_8 (and_8_out, counter_1_carry, ~or_2_out, Instruction_Enable);  // AND_Gate
  or or_4 (or_4_out, and_8_out, and_9_out);
  Counter counter_2 (
    .load(or_2_out), .D(multiplexer_1_out), .count(or_4_out), .Q(counter_2_q), .clk(CLK), .clr(and_6_out));  // open: carry
  assign DataOut = and_7_out ? {counter_2_q, counter_1_q} : 16'bz;  // Controlled_Buffer controlled_buffer_2
  and and_9 (and_9_out, counter_1_carry, and_4_out);

  // Notes on the sheet:
  //   mov reg,value16
  //   mov regH,value8
  //   mov regL,value8
  //   dec reg
  //   inc reg
  //   set 0
  //   Read/Write
endmodule

module BUS_Decoder_16_bit_bus_intruction_set_1 (
  input  CLK,
  input  [15:0] Data_In,
  output ax_enable_instruction,
  output [2:0] ax_instruction,
  output bx_enable_instruction,
  output [2:0] bx_instruction,
  output cx_enable_instruction,
  output [2:0] cx_instruction,
  output dx_enable_instruction,
  output [15:0] Control_Line_Out,
  output [2:0] dx_instruction,
  output RAM0_Instruction_Enable,
  output [7:0] RAM0_Instruction
);

  wire and_14_out, and_18_out, and_19_out, and_20_out, and_21_out, and_22_out, and_24_out, d_ff_1_q,
       d_ff_1_qn, d_ff_2_q, d_ff_2_qn, d_ff_3_q, d_ff_3_qn, d_ff_4_q, d_ff_4_qn, d_ff_5_q, d_ff_5_qn,
       d_ff_6_q, d_ff_6_qn, d_ff_7_q, d_ff_7_qn, d_ff_8_q, d_ff_8_qn, d_ff_9_q, d_ff_9_qn, d_ff_10_q,
       d_ff_10_qn, d_ff_11_q, d_ff_11_qn, d_ff_12_q, d_ff_12_qn, mov_ax_value16_out, mov_bx_value16_out,
       mov_cx_value16_out, mov_dx_value16_out, or_5_out, or_6_out, or_7_out, or_8_out, or_9_out, or_10_out,
       or_11_out, or_12_out, or_13_out, or_14_out, or_15_out, or_16_out, or_17_out, or_18_out, or_20_out,
       or_21_out, or_22_out;
  wire [2:2] and_1_out, and_3_out, and_5_out, and_13_out;
  wire [4:4] and_23_out;
  wire [5:4] and_7_out, and_9_out, and_11_out, and_15_out;
  wire [7:0] and_25_out, or_19_out;
  wire [15:0] and_26_out;

  assign ax_instruction = {3{and_13_out[2]}};  // OR_Gate or_1, 3 bits wide OR_Gate
  assign bx_instruction = {3{and_1_out[2]}};  // OR_Gate or_2, 3 bits wide OR_Gate
  assign cx_instruction = {3{and_3_out[2]}};  // OR_Gate or_3, 3 bits wide OR_Gate
  assign dx_instruction = {3{and_5_out[2]}};  // OR_Gate or_4, 3 bits wide OR_Gate
  and and_1 (and_1_out[2], ~bx_enable_instruction, or_13_out);  // AND_Gate
  and and_2 (cx_enable_instruction, or_14_out, d_ff_6_q);
  and and_3 (and_3_out[2], ~cx_enable_instruction, or_14_out);  // AND_Gate
  and and_4 (dx_enable_instruction, or_15_out, d_ff_7_q);
  and and_5 (and_5_out[2], ~dx_enable_instruction, or_15_out);  // AND_Gate
  and and_6 (bx_enable_instruction, or_13_out, d_ff_5_q);
  or or_5 (or_5_out, d_ff_10_q, d_ff_2_q);
  or or_6 (or_6_out, d_ff_11_q, d_ff_3_q);
  or or_7 (or_7_out, d_ff_12_q, d_ff_8_q, d_ff_4_q);
  or or_8 (or_8_out, d_ff_12_q, and_14_out);
  and and_7 (and_7_out[4], or_10_out, or_13_out);
  or or_9 (or_9_out, d_ff_9_q, d_ff_1_q);
  and and_8 (and_7_out[5], or_9_out, or_13_out);
  or or_10 (or_10_out, d_ff_1_q, d_ff_5_q);
  D_Flip_Flop d_ff_1 (.clk(CLK), .D(mov_bx_value16_out), .Q(d_ff_1_q), .Qn(d_ff_1_qn));  // open: preset, en, reset
  and and_9 (and_9_out[4], or_11_out, or_14_out);
  and and_10 (and_9_out[5], or_5_out, or_14_out);
  or or_11 (or_11_out, d_ff_2_q, d_ff_6_q);
  D_Flip_Flop d_ff_2 (.clk(CLK), .D(mov_cx_value16_out), .Q(d_ff_2_q), .Qn(d_ff_2_qn));  // open: preset, en, reset
  and and_11 (and_11_out[4], or_12_out, or_15_out);
  and and_12 (and_11_out[5], or_6_out, or_15_out);
  or or_12 (or_12_out, d_ff_3_q, d_ff_7_q);
  D_Flip_Flop d_ff_3 (.clk(CLK), .D(mov_dx_value16_out), .Q(d_ff_3_q), .Qn(d_ff_3_qn));  // open: preset, en, reset
  and and_13 (and_13_out[2], d_ff_8_q, ~ax_enable_instruction);  // AND_Gate
  D_Flip_Flop d_ff_4 (.clk(CLK), .D(mov_ax_value16_out), .Q(d_ff_4_q), .Qn(d_ff_4_qn));  // open: preset, en, reset
  and and_14 (and_14_out, ~d_ff_8_q, d_ff_4_q);  // AND_Gate
  and and_15 (and_15_out[4], or_16_out, or_7_out);
  and and_16 (and_15_out[5], or_8_out, or_7_out);
  or or_13 (or_13_out, d_ff_1_q, d_ff_5_q, d_ff_9_q);
  D_Flip_Flop d_ff_5 (.clk(CLK), .D(d_ff_1_q), .Q(d_ff_5_q), .Qn(d_ff_5_qn));  // open: preset, en, reset
  or or_14 (or_14_out, d_ff_2_q, d_ff_6_q, d_ff_10_q);
  D_Flip_Flop d_ff_6 (.clk(CLK), .D(d_ff_2_q), .Q(d_ff_6_q), .Qn(d_ff_6_qn));  // open: preset, en, reset
  or or_15 (or_15_out, d_ff_3_q, d_ff_7_q, d_ff_11_q);
  D_Flip_Flop d_ff_7 (.clk(CLK), .D(d_ff_3_q), .Q(d_ff_7_q), .Qn(d_ff_7_qn));  // open: preset, en, reset
  and and_17 (ax_enable_instruction, or_7_out, d_ff_8_q);
  D_Flip_Flop d_ff_8 (.clk(CLK), .D(d_ff_4_q), .Q(d_ff_8_q), .Qn(d_ff_8_qn));  // open: preset, en, reset
  or or_16 (or_16_out, d_ff_4_q, d_ff_8_q);
  D_Flip_Flop d_ff_9 (.clk(CLK), .D(d_ff_5_q), .Q(d_ff_9_q), .Qn(d_ff_9_qn));  // open: preset, en, reset
  or or_17 (or_17_out, d_ff_10_q, or_11_out, d_ff_2_q);
  D_Flip_Flop d_ff_10 (.clk(CLK), .D(d_ff_6_q), .Q(d_ff_10_q), .Qn(d_ff_10_qn));  // open: preset, en, reset
  and and_18 (and_18_out, d_ff_10_qn, d_ff_6_qn, d_ff_2_qn);
  or or_18 (or_18_out, d_ff_11_q, or_12_out, d_ff_3_q);
  D_Flip_Flop d_ff_11 (.clk(CLK), .D(d_ff_7_q), .Q(d_ff_11_q), .Qn(d_ff_11_qn));  // open: preset, en, reset
  and and_19 (and_19_out, d_ff_11_qn, d_ff_7_qn, d_ff_3_qn);
  D_Flip_Flop d_ff_12 (.clk(CLK), .D(d_ff_8_q), .Q(d_ff_12_q), .Qn(d_ff_12_qn));  // open: preset, en, reset
  and and_20 (and_20_out, d_ff_12_qn, d_ff_8_qn, d_ff_4_qn);
  assign or_19_out = {2'b00, and_15_out, and_15_out[4], 3'b000} | {2'b00, and_7_out, and_7_out[4], 3'b000} | {2'b00, and_9_out, and_9_out[4], 3'b000} | {2'b00, and_11_out, and_11_out[4], 3'b000};  // OR_Gate or_19, 8 bits wide
  or or_20 (or_20_out, d_ff_9_q, or_10_out, d_ff_1_q);
  and and_21 (and_21_out, d_ff_9_qn, d_ff_5_qn, d_ff_1_qn);
  buf and_22 (and_22_out, and_19_out);  // AND_Gate
  and mov_ax_value16 (mov_ax_value16_out, and_26_out[0], ~and_26_out[1], ~and_26_out[2], ~and_26_out[3], ~and_26_out[4], ~and_26_out[5], ~and_26_out[6], ~and_26_out[7], ~and_26_out[8], ~and_26_out[9], ~and_26_out[10], ~and_26_out[11], ~and_26_out[12], ~and_26_out[13], ~and_26_out[14], ~and_26_out[15]);  // AND_Gate
  and and_23 (and_23_out[4], and_20_out, and_21_out, and_24_out);
  or or_21 (or_21_out, d_ff_12_q, or_16_out);
  and mov_bx_value16 (mov_bx_value16_out, ~and_26_out[0], and_26_out[1], ~and_26_out[2], ~and_26_out[3], ~and_26_out[4], ~and_26_out[5], ~and_26_out[6], ~and_26_out[7], ~and_26_out[8], ~and_26_out[9], ~and_26_out[10], ~and_26_out[11], ~and_26_out[12], ~and_26_out[13], ~and_26_out[14], ~and_26_out[15]);  // AND_Gate
  and and_24 (and_24_out, and_22_out, and_18_out);
  and mov_cx_value16 (mov_cx_value16_out, and_26_out[0], and_26_out[1], ~and_26_out[2], ~and_26_out[3], ~and_26_out[4], ~and_26_out[5], ~and_26_out[6], ~and_26_out[7], ~and_26_out[8], ~and_26_out[9], ~and_26_out[10], ~and_26_out[11], ~and_26_out[12], ~and_26_out[13], ~and_26_out[14], ~and_26_out[15]);  // AND_Gate
  and mov_dx_value16 (mov_dx_value16_out, ~and_26_out[0], ~and_26_out[1], and_26_out[2], ~and_26_out[3], ~and_26_out[4], ~and_26_out[5], ~and_26_out[6], ~and_26_out[7], ~and_26_out[8], ~and_26_out[9], ~and_26_out[10], ~and_26_out[11], ~and_26_out[12], ~and_26_out[13], ~and_26_out[14], ~and_26_out[15]);  // AND_Gate
  or or_22 (or_22_out, or_21_out, or_20_out, or_17_out, or_18_out);
  assign and_25_out = 8'h18 & {3'b000, {2{and_23_out[4]}}, 3'b000};  // AND_Gate and_25, 8 bits wide
  assign and_26_out = {16{and_23_out[4]}} & Data_In;  // AND_Gate and_26, 16 bits wide
  or or_23 (RAM0_Instruction_Enable, and_23_out[4], or_22_out);
  assign RAM0_Instruction = and_25_out | or_19_out;  // OR_Gate or_24, 8 bits wide

  // Notes on the sheet:
  //   Combine the Enable with the instruction line
  //   When not exec inc RAM
  //   Combine the Enable in with the instruction line
endmodule

// Math Unit
module BUS_ALU (
  input  [15:0] BUS_In,
  input  Read_Write,
  input  CLK,
  input  Load_Enable,
  input  Load_Selector,
  input  Add_Sub,
  output [15:0] BUS_Out
);

  wire and_1_out, and_2_out, not_1_out;
  wire [15:0] adder_1_out, controlled_buffer_2_out, multiplexer_1_out, register_1_q, register_2_q,
       subtractor_1_out;

  assign BUS_Out = Read_Write ? multiplexer_1_out : 16'bz;  // Controlled_Buffer controlled_buffer_1
  assign controlled_buffer_2_out = not_1_out ? BUS_In : 16'bz;  // Controlled_Buffer controlled_buffer_2
  not not_1 (not_1_out, Read_Write);
  and and_1 (and_1_out, Load_Selector, Load_Enable);
  Register_part #(.width(16)) register_1 (
    .D(controlled_buffer_2_out), .en(and_1_out), .Q(register_1_q), .clk(CLK));  // open: clr
  Register_part #(.width(16)) register_2 (
    .D(controlled_buffer_2_out), .en(and_2_out), .Q(register_2_q), .clk(CLK));  // open: clr
  and and_2 (and_2_out, Load_Enable, ~Load_Selector);  // AND_Gate
  Adder #(.width(16)) adder_1 (.a(register_1_q), .b(register_2_q), .out(adder_1_out));  // open: cin, cout
  Subtractor #(.width(16)) subtractor_1 (
    .a(register_1_q), .b(register_2_q), .out(subtractor_1_out));  // open: bin, bout
  Multiplexer #(.width(16)) multiplexer_1 (
    .in0(adder_1_out), .in1(subtractor_1_out), .out(multiplexer_1_out), .sel(Add_Sub), .en(1'b1));
endmodule

module BUS_RAM (
  input  [15:0] Bus_In,
  input  CLK,
  input  [7:0] RAM_Instruction,
  input  RAM_Instruction_Enable,
  output [15:0] Bus_Out
);

  wire Inc_Address_out, jmp__data_out, Load_Temp_Address_out, mov_ip__ip_out, or_1_out, or_2_out, or_3_out,
       Read_To_BUS_At_IP_out, Read_Write_out, Store_at_IP_out, Use_Instruction_Pointer_Use_Temp_Address_out;
  wire [15:0] controlled_buffer_2_out, Instruction_Pointer_q, multiplexer_1_out, ram_1_data,
       Temp_Address_Pointer_q;

  and jmp__data (jmp__data_out, RAM_Instruction_Enable, RAM_Instruction[0]);
  and mov_ip__ip (mov_ip__ip_out, RAM_Instruction_Enable, RAM_Instruction[1]);
  and Store_at_IP (Store_at_IP_out, RAM_Instruction_Enable, RAM_Instruction[2]);
  and Read_To_BUS_At_IP (Read_To_BUS_At_IP_out, RAM_Instruction_Enable, RAM_Instruction[3]);
  and Read_Write (Read_Write_out, RAM_Instruction_Enable, RAM_Instruction[4]);
  and Inc_Address (Inc_Address_out, RAM_Instruction_Enable, RAM_Instruction[5]);
  and Load_Temp_Address (Load_Temp_Address_out, RAM_Instruction_Enable, RAM_Instruction[6]);
  nand Use_Instruction_Pointer_Use_Temp_Address (Use_Instruction_Pointer_Use_Temp_Address_out, RAM_Instruction_Enable, RAM_Instruction[7]);
  assign Bus_Out = Read_Write_out ? ram_1_data : 16'bz;  // Controlled_Buffer controlled_buffer_1
  assign controlled_buffer_2_out = mov_ip__ip_out ? ram_1_data : 16'bz;  // Controlled_Buffer controlled_buffer_2
  assign controlled_buffer_2_out = or_1_out ? Bus_In : 16'bz;  // Controlled_Buffer controlled_buffer_3
  or or_1 (or_1_out, Store_at_IP_out, Load_Temp_Address_out, jmp__data_out);
  Register_part #(.width(16)) Temp_Address_Pointer (
    .D(controlled_buffer_2_out), .en(Load_Temp_Address_out), .Q(Temp_Address_Pointer_q), .clk(CLK));  // open: clr
  or or_2 (or_2_out, jmp__data_out, mov_ip__ip_out);
  Counter #(.width(16), .max('hffff)) Instruction_Pointer (
    .load(or_2_out), .D(controlled_buffer_2_out), .count(Inc_Address_out), .Q(Instruction_Pointer_q),
    .clk(CLK));  // open: carry, clr
  Multiplexer #(.width(16), .enable("false")) multiplexer_1 (
    .in0(Temp_Address_Pointer_q), .in1(Instruction_Pointer_q), .out(multiplexer_1_out),
    .sel(Use_Instruction_Pointer_Use_Temp_Address_out));
  or or_3 (or_3_out, mov_ip__ip_out, Read_To_BUS_At_IP_out);
  RAM #(.addrWidth(16), .dataWidth(16), .bus("separate")) ram_1 (
    .addr(multiplexer_1_out), .din(controlled_buffer_2_out), .data(ram_1_data), .str(Store_at_IP_out),
    .clk(CLK), .ld(or_3_out));  // open: sel, clr
endmodule

module BUS_GPU (
  input  [15:0] Bus_In,
  input  CLK,
  input  Set_Pixel_Bank,
  input  Bank_Selector,
  output [15:0] Bus_Out
);

  wire and_1_out, decoder_1_out0, decoder_1_out1, decoder_1_out2, decoder_1_out3, decoder_1_out4,
       decoder_1_out5, decoder_1_out6, decoder_1_out7, decoder_1_out8, decoder_1_out9, decoder_1_out10,
       decoder_1_out11, decoder_1_out12, decoder_1_out13, decoder_1_out14, decoder_1_out15, decoder_1_out16,
       decoder_1_out17, decoder_1_out18, decoder_1_out19, decoder_1_out20, decoder_1_out21, decoder_1_out22,
       decoder_1_out23, decoder_1_out24, decoder_1_out25, decoder_1_out26, decoder_1_out27, decoder_1_out28,
       decoder_1_out29, decoder_1_out30, decoder_1_out31, decoder_2_out0, decoder_2_out1, decoder_2_out2,
       decoder_2_out3, decoder_2_out4, decoder_2_out5, decoder_2_out6, decoder_2_out7, decoder_2_out8,
       decoder_2_out9, decoder_2_out10, decoder_2_out11, decoder_2_out12, decoder_2_out13, decoder_2_out14,
       decoder_2_out15, decoder_2_out16, decoder_2_out17, decoder_2_out18, decoder_2_out19, decoder_2_out20,
       decoder_2_out21, decoder_2_out22, decoder_2_out23, decoder_2_out24, decoder_2_out25, decoder_2_out26,
       decoder_2_out27, decoder_2_out28, decoder_2_out29, decoder_2_out30, decoder_2_out31, undriven;
  wire [4:0] controlled_buffer_2_out, register_1_q, register_2_q;
  wire [15:0] undriven_2;
  wire [15:5] controlled_buffer_2_out_2;
  wire [31:0] bus_gpu_register_1_out_5, bus_gpu_register_2_out_5, bus_gpu_register_3_out_5,
       bus_gpu_register_4_out_5, bus_gpu_register_5_out_5, bus_gpu_register_6_out_5,
       bus_gpu_register_7_out_5, bus_gpu_register_8_out_5, bus_gpu_register_9_out_5,
       bus_gpu_register_10_out_5, bus_gpu_register_11_out_5, bus_gpu_register_12_out_5,
       bus_gpu_register_13_out_5, bus_gpu_register_14_out_5, bus_gpu_register_15_out_5,
       bus_gpu_register_16_out_5, bus_gpu_register_17_out_5, bus_gpu_register_18_out_5,
       bus_gpu_register_19_out_5, bus_gpu_register_20_out_5, bus_gpu_register_21_out_5,
       bus_gpu_register_22_out_5, bus_gpu_register_23_out_5, bus_gpu_register_24_out_5,
       bus_gpu_register_25_out_5, bus_gpu_register_26_out_5, bus_gpu_register_27_out_5,
       bus_gpu_register_28_out_5, bus_gpu_register_29_out_5, bus_gpu_register_30_out_5,
       bus_gpu_register_31_out_5, bus_gpu_register_32_out_5;

  assign Bus_Out = undriven ? undriven_2 : 16'bz;  // Controlled_Buffer controlled_buffer_1
  assign {controlled_buffer_2_out_2, controlled_buffer_2_out} = Set_Pixel_Bank ? Bus_In : 16'bz;  // Controlled_Buffer controlled_buffer_2
  Register_part #(.width(5)) register_1 (
    .D(controlled_buffer_2_out), .en(Bank_Selector), .Q(register_1_q), .clk(CLK));  // open: clr
  Decoder_part #(.select(5), .enable("false")) decoder_1 (
    .out0(decoder_1_out0), .out1(decoder_1_out1), .out2(decoder_1_out2), .out3(decoder_1_out3),
    .out4(decoder_1_out4), .out5(decoder_1_out5), .out6(decoder_1_out6), .out7(decoder_1_out7),
    .out8(decoder_1_out8), .out9(decoder_1_out9), .out10(decoder_1_out10), .out11(decoder_1_out11),
    .out12(decoder_1_out12), .out13(decoder_1_out13), .out14(decoder_1_out14), .out15(decoder_1_out15),
    .out16(decoder_1_out16), .out17(decoder_1_out17), .out18(decoder_1_out18), .out19(decoder_1_out19),
    .out20(decoder_1_out20), .out21(decoder_1_out21), .out22(decoder_1_out22), .out23(decoder_1_out23),
    .out24(decoder_1_out24), .out25(decoder_1_out25), .out26(decoder_1_out26), .out27(decoder_1_out27),
    .out28(decoder_1_out28), .out29(decoder_1_out29), .out30(decoder_1_out30), .out31(decoder_1_out31),
    .sel(register_1_q));
  and and_1 (and_1_out, Set_Pixel_Bank, ~Bank_Selector);  // AND_Gate
  Register_part #(.width(5)) register_2 (
    .D(controlled_buffer_2_out), .en(and_1_out), .Q(register_2_q), .clk(CLK));  // open: clr
  Decoder_part #(.select(5), .enable("false")) decoder_2 (
    .out0(decoder_2_out0), .out1(decoder_2_out1), .out2(decoder_2_out2), .out3(decoder_2_out3),
    .out4(decoder_2_out4), .out5(decoder_2_out5), .out6(decoder_2_out6), .out7(decoder_2_out7),
    .out8(decoder_2_out8), .out9(decoder_2_out9), .out10(decoder_2_out10), .out11(decoder_2_out11),
    .out12(decoder_2_out12), .out13(decoder_2_out13), .out14(decoder_2_out14), .out15(decoder_2_out15),
    .out16(decoder_2_out16), .out17(decoder_2_out17), .out18(decoder_2_out18), .out19(decoder_2_out19),
    .out20(decoder_2_out20), .out21(decoder_2_out21), .out22(decoder_2_out22), .out23(decoder_2_out23),
    .out24(decoder_2_out24), .out25(decoder_2_out25), .out26(decoder_2_out26), .out27(decoder_2_out27),
    .out28(decoder_2_out28), .out29(decoder_2_out29), .out30(decoder_2_out30), .out31(decoder_2_out31),
    .sel(register_2_q));
  DotMatrix #(.matrixcols(32), .matrixrows(32)) dotmatrix_1 (
    .col0(bus_gpu_register_1_out_5), .col1(bus_gpu_register_2_out_5), .col2(bus_gpu_register_3_out_5),
    .col3(bus_gpu_register_4_out_5), .col4(bus_gpu_register_5_out_5), .col5(bus_gpu_register_6_out_5),
    .col6(bus_gpu_register_7_out_5), .col7(bus_gpu_register_8_out_5), .col8(bus_gpu_register_9_out_5),
    .col9(bus_gpu_register_10_out_5), .col10(bus_gpu_register_11_out_5), .col11(bus_gpu_register_12_out_5),
    .col12(bus_gpu_register_13_out_5), .col13(bus_gpu_register_14_out_5), .col14(bus_gpu_register_15_out_5),
    .col15(bus_gpu_register_16_out_5), .col16(bus_gpu_register_17_out_5), .col17(bus_gpu_register_18_out_5),
    .col18(bus_gpu_register_19_out_5), .col19(bus_gpu_register_20_out_5), .col20(bus_gpu_register_21_out_5),
    .col21(bus_gpu_register_22_out_5), .col22(bus_gpu_register_23_out_5), .col23(bus_gpu_register_24_out_5),
    .col24(bus_gpu_register_25_out_5), .col25(bus_gpu_register_26_out_5), .col26(bus_gpu_register_27_out_5),
    .col27(bus_gpu_register_28_out_5), .col28(bus_gpu_register_29_out_5), .col29(bus_gpu_register_30_out_5),
    .col30(bus_gpu_register_31_out_5), .col31(bus_gpu_register_32_out_5));
  BUS_GPU_Register bus_gpu_register_1 (
    .Data_In({controlled_buffer_2_out_2, controlled_buffer_2_out}), .CLK(CLK), .Write_Enable(decoder_1_out0),
    .Write_Select(decoder_2_out0), .out_5(bus_gpu_register_1_out_5));
  BUS_GPU_Register bus_gpu_register_2 (
    .Data_In({controlled_buffer_2_out_2, controlled_buffer_2_out}), .CLK(CLK), .Write_Enable(decoder_1_out1),
    .Write_Select(decoder_2_out1), .out_5(bus_gpu_register_2_out_5));
  BUS_GPU_Register bus_gpu_register_3 (
    .Data_In({controlled_buffer_2_out_2, controlled_buffer_2_out}), .CLK(CLK), .Write_Enable(decoder_1_out2),
    .Write_Select(decoder_2_out2), .out_5(bus_gpu_register_3_out_5));
  BUS_GPU_Register bus_gpu_register_4 (
    .Data_In({controlled_buffer_2_out_2, controlled_buffer_2_out}), .CLK(CLK), .Write_Enable(decoder_1_out3),
    .Write_Select(decoder_2_out3), .out_5(bus_gpu_register_4_out_5));
  BUS_GPU_Register bus_gpu_register_5 (
    .Data_In({controlled_buffer_2_out_2, controlled_buffer_2_out}), .CLK(CLK), .Write_Enable(decoder_1_out4),
    .Write_Select(decoder_2_out4), .out_5(bus_gpu_register_5_out_5));
  BUS_GPU_Register bus_gpu_register_6 (
    .Data_In({controlled_buffer_2_out_2, controlled_buffer_2_out}), .CLK(CLK), .Write_Enable(decoder_1_out5),
    .Write_Select(decoder_2_out5), .out_5(bus_gpu_register_6_out_5));
  BUS_GPU_Register bus_gpu_register_7 (
    .Data_In({controlled_buffer_2_out_2, controlled_buffer_2_out}), .CLK(CLK), .Write_Enable(decoder_1_out6),
    .Write_Select(decoder_2_out6), .out_5(bus_gpu_register_7_out_5));
  BUS_GPU_Register bus_gpu_register_8 (
    .Data_In({controlled_buffer_2_out_2, controlled_buffer_2_out}), .CLK(CLK), .Write_Enable(decoder_1_out7),
    .Write_Select(decoder_2_out7), .out_5(bus_gpu_register_8_out_5));
  BUS_GPU_Register bus_gpu_register_9 (
    .Data_In({controlled_buffer_2_out_2, controlled_buffer_2_out}), .CLK(CLK), .Write_Enable(decoder_1_out8),
    .Write_Select(decoder_2_out8), .out_5(bus_gpu_register_9_out_5));
  BUS_GPU_Register bus_gpu_register_10 (
    .Data_In({controlled_buffer_2_out_2, controlled_buffer_2_out}), .CLK(CLK), .Write_Enable(decoder_1_out9),
    .Write_Select(decoder_2_out9), .out_5(bus_gpu_register_10_out_5));
  BUS_GPU_Register bus_gpu_register_11 (
    .Data_In({controlled_buffer_2_out_2, controlled_buffer_2_out}), .CLK(CLK),
    .Write_Enable(decoder_1_out10), .Write_Select(decoder_2_out10), .out_5(bus_gpu_register_11_out_5));
  BUS_GPU_Register bus_gpu_register_12 (
    .Data_In({controlled_buffer_2_out_2, controlled_buffer_2_out}), .CLK(CLK),
    .Write_Enable(decoder_1_out11), .Write_Select(decoder_2_out11), .out_5(bus_gpu_register_12_out_5));
  BUS_GPU_Register bus_gpu_register_13 (
    .Data_In({controlled_buffer_2_out_2, controlled_buffer_2_out}), .CLK(CLK),
    .Write_Enable(decoder_1_out12), .Write_Select(decoder_2_out12), .out_5(bus_gpu_register_13_out_5));
  BUS_GPU_Register bus_gpu_register_14 (
    .Data_In({controlled_buffer_2_out_2, controlled_buffer_2_out}), .CLK(CLK),
    .Write_Enable(decoder_1_out13), .Write_Select(decoder_2_out13), .out_5(bus_gpu_register_14_out_5));
  BUS_GPU_Register bus_gpu_register_15 (
    .Data_In({controlled_buffer_2_out_2, controlled_buffer_2_out}), .CLK(CLK),
    .Write_Enable(decoder_1_out14), .Write_Select(decoder_2_out14), .out_5(bus_gpu_register_15_out_5));
  BUS_GPU_Register bus_gpu_register_16 (
    .Data_In({controlled_buffer_2_out_2, controlled_buffer_2_out}), .CLK(CLK),
    .Write_Enable(decoder_1_out15), .Write_Select(decoder_2_out15), .out_5(bus_gpu_register_16_out_5));
  BUS_GPU_Register bus_gpu_register_17 (
    .Data_In({controlled_buffer_2_out_2, controlled_buffer_2_out}), .CLK(CLK),
    .Write_Enable(decoder_1_out16), .Write_Select(decoder_2_out16), .out_5(bus_gpu_register_17_out_5));
  BUS_GPU_Register bus_gpu_register_18 (
    .Data_In({controlled_buffer_2_out_2, controlled_buffer_2_out}), .CLK(CLK),
    .Write_Enable(decoder_1_out17), .Write_Select(decoder_2_out17), .out_5(bus_gpu_register_18_out_5));
  BUS_GPU_Register bus_gpu_register_19 (
    .Data_In({controlled_buffer_2_out_2, controlled_buffer_2_out}), .CLK(CLK),
    .Write_Enable(decoder_1_out18), .Write_Select(decoder_2_out18), .out_5(bus_gpu_register_19_out_5));
  BUS_GPU_Register bus_gpu_register_20 (
    .Data_In({controlled_buffer_2_out_2, controlled_buffer_2_out}), .CLK(CLK),
    .Write_Enable(decoder_1_out19), .Write_Select(decoder_2_out19), .out_5(bus_gpu_register_20_out_5));
  BUS_GPU_Register bus_gpu_register_21 (
    .Data_In({controlled_buffer_2_out_2, controlled_buffer_2_out}), .CLK(CLK),
    .Write_Enable(decoder_1_out20), .Write_Select(decoder_2_out20), .out_5(bus_gpu_register_21_out_5));
  BUS_GPU_Register bus_gpu_register_22 (
    .Data_In({controlled_buffer_2_out_2, controlled_buffer_2_out}), .CLK(CLK),
    .Write_Enable(decoder_1_out21), .Write_Select(decoder_2_out21), .out_5(bus_gpu_register_22_out_5));
  BUS_GPU_Register bus_gpu_register_23 (
    .Data_In({controlled_buffer_2_out_2, controlled_buffer_2_out}), .CLK(CLK),
    .Write_Enable(decoder_1_out22), .Write_Select(decoder_2_out22), .out_5(bus_gpu_register_23_out_5));
  BUS_GPU_Register bus_gpu_register_24 (
    .Data_In({controlled_buffer_2_out_2, controlled_buffer_2_out}), .CLK(CLK),
    .Write_Enable(decoder_1_out23), .Write_Select(decoder_2_out23), .out_5(bus_gpu_register_24_out_5));
  BUS_GPU_Register bus_gpu_register_25 (
    .Data_In({controlled_buffer_2_out_2, controlled_buffer_2_out}), .CLK(CLK),
    .Write_Enable(decoder_1_out24), .Write_Select(decoder_2_out24), .out_5(bus_gpu_register_25_out_5));
  BUS_GPU_Register bus_gpu_register_26 (
    .Data_In({controlled_buffer_2_out_2, controlled_buffer_2_out}), .CLK(CLK),
    .Write_Enable(decoder_1_out25), .Write_Select(decoder_2_out25), .out_5(bus_gpu_register_26_out_5));
  BUS_GPU_Register bus_gpu_register_27 (
    .Data_In({controlled_buffer_2_out_2, controlled_buffer_2_out}), .CLK(CLK),
    .Write_Enable(decoder_1_out26), .Write_Select(decoder_2_out26), .out_5(bus_gpu_register_27_out_5));
  BUS_GPU_Register bus_gpu_register_28 (
    .Data_In({controlled_buffer_2_out_2, controlled_buffer_2_out}), .CLK(CLK),
    .Write_Enable(decoder_1_out27), .Write_Select(decoder_2_out27), .out_5(bus_gpu_register_28_out_5));
  BUS_GPU_Register bus_gpu_register_29 (
    .Data_In({controlled_buffer_2_out_2, controlled_buffer_2_out}), .CLK(CLK),
    .Write_Enable(decoder_1_out28), .Write_Select(decoder_2_out28), .out_5(bus_gpu_register_29_out_5));
  BUS_GPU_Register bus_gpu_register_30 (
    .Data_In({controlled_buffer_2_out_2, controlled_buffer_2_out}), .CLK(CLK),
    .Write_Enable(decoder_1_out29), .Write_Select(decoder_2_out29), .out_5(bus_gpu_register_30_out_5));
  BUS_GPU_Register bus_gpu_register_31 (
    .Data_In({controlled_buffer_2_out_2, controlled_buffer_2_out}), .CLK(CLK),
    .Write_Enable(decoder_1_out30), .Write_Select(decoder_2_out30), .out_5(bus_gpu_register_31_out_5));
  BUS_GPU_Register bus_gpu_register_32 (
    .Data_In({controlled_buffer_2_out_2, controlled_buffer_2_out}), .CLK(CLK),
    .Write_Enable(decoder_1_out31), .Write_Select(decoder_2_out31), .out_5(bus_gpu_register_32_out_5));
endmodule

module BUS_GPU_Register (
  input  [15:0] Data_In,
  input  CLK,
  input  Write_Enable,
  input  Write_Select,
  output [31:0] out_5
);

  wire and_1_out, and_2_out;

  and and_1 (and_1_out, Write_Enable, ~Write_Select);  // AND_Gate
  and and_2 (and_2_out, Write_Enable, Write_Select);
  Register_part #(.width(16)) register_1 (.D(Data_In), .en(and_1_out), .Q(out_5[15:0]), .clk(CLK));  // open: clr
  Register_part #(.width(16)) register_2 (.D(Data_In), .en(and_2_out), .Q(out_5[31:16]), .clk(CLK));  // open: clr
endmodule
